// Logisim project Aniol64keyboard.circ as structural Verilog: 1 circuit, main circuit main
module main (
  input  in_1,
  input  M1,
  input  IORQ,
  input  IEI,
  input  RD,
  input  IORQ_2,
  input  A2,
  input  D0,
  input  WR,
  output IEO,
  output [6:0] out_11,
  output Register_OE_prime,
  output INT
);

  wire and_1_out, and_2_out, buzzer_1_p3, buzzer_1_p4, clock_1_out, d_ff_1_q, d_ff_2_q, d_ff_2_qn, not_1_out,
       or_1_out, or_2_out, or_3_out, or_4_out, pull_resistor_1_node, switch_1_p1, switch_1_p2, switch_1_p4,
       switch_1_p5, switch_1_p6;
  wire [6:0] counter_1_q;

  Clock clock_1 (.out(clock_1_out));
  Pull_Resistor #(.pull(1)) pull_resistor_1 (.node(pull_resistor_1_node));
  or or_1 (or_1_out, IORQ_2, A2);
  Counter #(.max('h7f), .width(7)) counter_1 (
    .clr(in_1), .clk(and_1_out), .Q(counter_1_q));  // open: load, up, count, D, carry
  and and_1 (and_1_out, clock_1_out, pull_resistor_1_node);
  or or_2 (or_2_out, RD, or_1_out);
  or or_3 (or_3_out, or_1_out, WR);
  Register #(.width(7)) register_1 (.D(counter_1_q), .clk(and_2_out), .Q(out_11));  // open: en, clr
  D_Flip_Flop d_ff_1 (.D(D0), .clk(or_3_out), .Q(d_ff_1_q));  // open: Qn, preset, reset
  Multiplexer #(.enable("false"), .select(3)) multiplexer_1 (
    .in2(switch_1_p5), .out(pull_resistor_1_node), .sel(counter_1_q[6:4]));  // open: in0, in1, in3, in4, in5, in6, in7
  LED led_1 (.in(pull_resistor_1_node));
  // Buzzer buzzer_1: pin names not known; wires that end beside it: or_2_out, Register_OE_prime, buzzer_1_p3, buzzer_1_p4
  Transistor transistor_1 (.in(buzzer_1_p4), .out(buzzer_1_p3), .gate(d_ff_1_q));
  or or_4 (or_4_out, M1, IORQ);
  D_Flip_Flop d_ff_2 (
    .D(1'b1), .clk(pull_resistor_1_node), .Q(d_ff_2_q), .Qn(d_ff_2_qn), .reset(not_1_out));  // open: preset
  not not_1 (not_1_out, or_4_out);
  // Switch switch_1: pin names not known; wires that end beside it: switch_1_p1, switch_1_p2, switch_1_p1, switch_1_p4, switch_1_p5, switch_1_p6, switch_1_p6
  and and_2 (and_2_out, d_ff_2_q, IEI);
  Demultiplexer #(.enable("false"), .select(4)) demultiplexer_1 (
    .out0(switch_1_p2), .out3(switch_1_p4), .in(1'b1), .sel(counter_1_q[3:0]));  // open: out1, out2, out4, out5, out6, out7, out8, out9, out10, out11, out12, out13, out14, out15
  and and_3 (IEO, d_ff_2_qn, IEI);
  not not_2 (INT, and_2_out);
  // also tied to GND on the sheet: buzzer_1_p3

  // Notes on the sheet:
  //   Interrupt Acknowledge
  //   D6-D0
endmodule
