// Logisim project VGA.circ as structural Verilog: 1 circuit, main circuit main
module main (
  output VGA_out
);

  wire clock_1_out;

  Clock clock_1 (.out(clock_1_out));
  Counter #(.max('h1ff), .width(9)) counter_1 (.clk(clock_1_out));  // open: clr, load, up, count, D, carry, Q
  RAM #(.addrWidth(11)) ram_1 ();  // open: addr, we, oe, clk, din, dout
  Counter counter_2 ();  // open: clr, load, up, count, clk, D, carry, Q
  ROM #(.addrWidth(11)) rom_1 ();  // open: addr, data
  // Shift_Register shift_register_1: pin names not known; wires that end beside it: clock_1_out, VGA_out

  // Notes on the sheet:
  //   X counter
  //   Image RAM
  //   Y counter
  //   Character ROM
endmodule
